// Logisim project circuito-jk.circ as structural Verilog: 1 circuit, main circuit main
module main (
  input  X
);

  wire and_1_out, and_2_out, and_3_out, and_4_out, and_5_out, clock_1_out, j_k_ff_1_q, j_k_ff_2_q,
       j_k_ff_2_qn, j_k_ff_3_q, j_k_ff_3_qn, not_1_out, not_2_out, not_3_out, not_4_out, or_1_out;

  not not_1 (not_1_out, X);
  and and_1 (and_1_out, j_k_ff_2_qn, j_k_ff_3_q, not_1_out);
  and and_2 (and_2_out, j_k_ff_1_q, j_k_ff_3_qn, X);
  and and_3 (and_3_out, j_k_ff_2_q, j_k_ff_3_qn, X);
  and and_4 (and_4_out, j_k_ff_2_q, j_k_ff_3_q);
  not not_2 (not_2_out, or_1_out);
  or or_1 (or_1_out, and_1_out, and_2_out, and_3_out);
  and and_5 (and_5_out, j_k_ff_2_q, j_k_ff_3_q);
  Clock clock_1 (.out(clock_1_out));
  J_K_Flip_Flop j_k_ff_1 (
    .J(and_4_out), .clk(clock_1_out), .K(not_3_out), .Q(j_k_ff_1_q));  // open: Qn, preset, en, reset
  not not_3 (not_3_out, and_4_out);
  J_K_Flip_Flop j_k_ff_2 (
    .J(or_1_out), .clk(clock_1_out), .K(not_2_out), .Q(j_k_ff_2_q), .Qn(j_k_ff_2_qn));  // open: preset, en, reset
  J_K_Flip_Flop j_k_ff_3 (
    .J(X), .clk(clock_1_out), .K(not_4_out), .Q(j_k_ff_3_q), .Qn(j_k_ff_3_qn));  // open: preset, en, reset
  not not_4 (not_4_out, X);
  // Probe on and_5_out

  // Notes on the sheet:
  //   D
  //   E
  //   F
  //   Y
  //   A
  //   B
  //   C
endmodule
