// Logisim project circuito.circ as structural Verilog: 1 circuit, main circuit main
module main (
  input  X
);

  wire and_1_out, and_2_out, and_3_out, and_4_out, and_5_out, clock_1_out, d_ff_1_q, d_ff_2_q, d_ff_2_qn,
       d_ff_3_q, d_ff_3_qn, not_1_out, or_1_out;

  not not_1 (not_1_out, X);
  and and_1 (and_1_out, d_ff_2_qn, d_ff_3_q, not_1_out);
  and and_2 (and_2_out, d_ff_1_q, d_ff_3_qn, X);
  and and_3 (and_3_out, d_ff_2_q, d_ff_3_qn, X);
  and and_4 (and_4_out, d_ff_2_q, d_ff_3_q);
  or or_1 (or_1_out, and_1_out, and_2_out, and_3_out);
  and and_5 (and_5_out, d_ff_2_q, d_ff_3_q);
  Clock clock_1 (.out(clock_1_out));
  D_Flip_Flop d_ff_1 (.clk(clock_1_out), .D(and_4_out), .Q(d_ff_1_q));  // open: Qn, preset, en, reset
  D_Flip_Flop d_ff_2 (.clk(clock_1_out), .D(or_1_out), .Q(d_ff_2_q), .Qn(d_ff_2_qn));  // open: preset, en, reset
  D_Flip_Flop d_ff_3 (.clk(clock_1_out), .D(X), .Q(d_ff_3_q), .Qn(d_ff_3_qn));  // open: preset, en, reset
  // Probe on and_5_out

  // Notes on the sheet:
  //   D
  //   E
  //   F
  //   Y
  //   A
  //   B
  //   C
endmodule
